// Logisim project logisim.circ as structural Verilog: 18 circuits, main circuit main
// Instruction Register
module main (
);

  wire ALU_carry, ALU_set_carry, and_1_out, buffer_1_out, buffer_2_out, Carry_out, Clock_out, CU_accu_to_bus,
       CU_bus_to_accu, CU_bus_to_m1, CU_bus_to_m2, CU_bus_to_p1, CU_bus_to_p2, CU_bus_to_ram, CU_increment_p,
       CU_ram_select_p, CU_ram_to_bus, CU_zero_bus, not_1_out, or_1_out, or_2_out, or_3_out, Reset_out;
  wire [2:0] CU_alu;
  wire [3:0] Accu_output, Accu_output_2;
  wire [7:0] ALU_accumulator_2, CU_bus_out, multiplexer_1_out, ram_1_data;
  wire [15:0] controlled_buffer_1_out, M2_output, Program_Counter_mem_out;

  Button Reset (.out(Reset_out));
  Clock Clock (.out(Clock_out));
  or or_1 (or_1_out, ~CU_bus_to_ram, CU_ram_to_bus);  // OR_Gate
  RAM #(.addrWidth(16), .bus("asynch")) ram_1 (
    .addr(controlled_buffer_1_out), .data(ram_1_data), .ld(or_1_out), .clr(Reset_out));  // open: sel
  assign controlled_buffer_1_out = CU_ram_select_p ? Program_Counter_mem_out : 16'bz;  // Controlled_Buffer controlled_buffer_1
  assign controlled_buffer_1_out = not_1_out ? M2_output : 16'bz;  // Controlled_Buffer controlled_buffer_2
  not not_1 (not_1_out, CU_ram_select_p);
  Control_Unit CU (
    .Reset(Reset_out), .Clock(Clock_out), .BUS_in(CU_bus_out), .Bus_To_RAM(CU_bus_to_ram),
    .RAM_to_Bus(CU_ram_to_bus), .RAM_select_P(CU_ram_select_p), .Increment_P(CU_increment_p),
    .Bus_To_M1(CU_bus_to_m1), .Bus_To_M2(CU_bus_to_m2), .Bus_To_P1(CU_bus_to_p1), .Bus_To_P2(CU_bus_to_p2),
    .Accu_to_Bus(CU_accu_to_bus), .Bus_to_Accu(CU_bus_to_accu), .Zero_Bus(CU_zero_bus), .ALU(CU_alu),
    .BUS_out(CU_bus_out));  // open: Empty, Empty_2
  Program_Counter Program_Counter (
    .BUS_to_P2(CU_bus_to_p2), .BUS_in(CU_bus_out), .Increment(CU_increment_p), .Bus_to_P1(CU_bus_to_p1),
    .Mem_Out(Program_Counter_mem_out));
  MemoryCell M2 (.Input(CU_bus_out), .Set(CU_bus_to_m2), .Output(M2_output[7:0]));
  MemoryCell M1 (.Input(CU_bus_out), .Set(CU_bus_to_m1), .Output(M2_output[15:8]));
  Hex_Digit_Display hex_digit_display_1 (.value(Program_Counter_mem_out[3:0]));  // open: dp
  assign CU_bus_out = CU_ram_to_bus ? ram_1_data : 8'bz;  // Controlled_Buffer controlled_buffer_3
  assign ram_1_data = CU_bus_to_ram ? CU_bus_out : 8'bz;  // Controlled_Buffer controlled_buffer_4
  Hex_Digit_Display hex_digit_display_2 (.value(Program_Counter_mem_out[7:4]));  // open: dp
  Hex_Digit_Display hex_digit_display_3 (.value(Program_Counter_mem_out[15:12]));  // open: dp
  Hex_Digit_Display hex_digit_display_4 (.value(Program_Counter_mem_out[11:8]));  // open: dp
  Multiplexer #(.width(8), .enable("false")) multiplexer_1 (
    .in0(ALU_accumulator_2), .in1(CU_bus_out), .out(multiplexer_1_out), .sel(CU_bus_to_accu));
  assign CU_bus_out = CU_accu_to_bus ? {Accu_output_2, Accu_output} : 8'bz;  // Controlled_Buffer controlled_buffer_5
  MemoryCell Accu (.Input(multiplexer_1_out), .Set(or_2_out), .Output({Accu_output_2, Accu_output}));
  or or_2 (or_2_out, Clock_out, CU_bus_to_accu);
  and and_1 (and_1_out, Clock_out, ALU_set_carry);
  ALU ALU (
    .Accumulator({Accu_output_2, Accu_output}), .Control_Unit(CU_alu), .BUS(CU_bus_out), .Carry(ALU_carry),
    .Accumulator_2(ALU_accumulator_2), .Set_Carry(ALU_set_carry));
  assign CU_bus_out = buffer_1_out ? {8{1'b0}} : 8'bz;  // Controlled_Buffer controlled_buffer_6
  buf buffer_1 (buffer_1_out, buffer_2_out);
  buf buffer_2 (buffer_2_out, CU_zero_bus);
  buf buffer_3 (buffer_1_out, CU_zero_bus);
  Hex_Digit_Display hex_digit_display_5 (.value(Accu_output_2));  // open: dp
  or or_3 (or_3_out, and_1_out, Reset_out);
  Hex_Digit_Display hex_digit_display_6 (.value(CU_bus_out[7:4]));  // open: dp
  Hex_Digit_Display hex_digit_display_7 (.value(Accu_output));  // open: dp
  MS_D_Latch Carry (.Input(ALU_carry), .Clock(or_3_out), .Out(Carry_out));  // open: Out_negate
  LED led_1 (.in(Carry_out));
  Hex_Digit_Display hex_digit_display_8 (.value(CU_bus_out[3:0]));  // open: dp
endmodule

module Control_Unit (
  input  Reset,
  input  Clock,
  input  [7:0] BUS_in,
  output Bus_To_RAM,
  output RAM_to_Bus,
  output RAM_select_P,
  output Increment_P,
  output Bus_To_M1,
  output Bus_To_M2,
  output Bus_To_P1,
  output Bus_To_P2,
  output Accu_to_Bus,
  output Bus_to_Accu,
  output Zero_Bus,
  output Empty,
  output Empty_2,
  output [2:0] ALU,
  output [7:0] BUS_out
);

  wire controlled_buffer_1_out, halfadder_1_carry, halfadder_1_sum, halfadder_2_carry, halfadder_2_sum,
       or_1_out;
  wire [1:0] ms_d_latch_1_out;
  wire [7:0] IR_output, multiplexer_1_out;

  assign controlled_buffer_1_out = or_1_out ? Clock : 1'bz;  // Controlled_Buffer controlled_buffer_1
  Multiplexer #(.width(8), .enable("false")) multiplexer_1 (
    .in0(BUS_in), .in1({8{1'b1}}), .out(multiplexer_1_out), .sel(Reset));
  HalfAdder halfadder_1 (.A(1'b1), .B(ms_d_latch_1_out[0]), .Sum(halfadder_1_sum), .Carry(halfadder_1_carry));
  MS_D_Latch ms_d_latch_1 (.Input(halfadder_1_sum), .Clock(Clock), .Out(ms_d_latch_1_out[0]));  // open: Out_negate
  or or_1 (or_1_out, Reset, halfadder_2_carry);
  HalfAdder halfadder_2 (
    .A(halfadder_1_carry), .B(ms_d_latch_1_out[1]), .Sum(halfadder_2_sum), .Carry(halfadder_2_carry));
  MS_D_Latch ms_d_latch_2 (.Input(halfadder_2_sum), .Clock(Clock), .Out(ms_d_latch_1_out[1]));  // open: Out_negate
  MemoryCell IR (.Input(multiplexer_1_out), .Set(controlled_buffer_1_out), .Output(IR_output));
  ROM #(.dataWidth(16)) rom_1 (
    .addr({IR_output[5:0], ms_d_latch_1_out}),
    .data({ALU, Empty_2, Empty, Zero_Bus, Bus_to_Accu, Accu_to_Bus, Bus_To_P2, Bus_To_P1, Bus_To_M2, Bus_To_M1, Increment_P, RAM_select_P, RAM_to_Bus, Bus_To_RAM}));  // open: sel
  Controlled_Buffer #(.width(8)) controlled_buffer_2 (.out(BUS_out));  // open: in, en

  // Notes on the sheet:
  //   contents of rom_1 (hex, n*v repeats v):
  //   252*0 4*6f0
endmodule

module Program_Counter (
  input  BUS_to_P2,
  input  [7:0] BUS_in,
  input  Increment,
  input  Bus_to_P1,
  output [15:0] Mem_Out
);

  wire buffer_1_out, buffer_2_out, buffer_3_out, buffer_4_out, buffer_5_out, buffer_6_out, buffer_7_out,
       buffer_8_out, buffer_9_out, buffer_10_out, buffer_11_out, buffer_12_out, buffer_13_out, buffer_14_out,
       buffer_15_out, buffer_16_out, controlled_buffer_1_out, halfadder_1_carry, halfadder_1_sum,
       halfadder_2_carry, halfadder_2_sum, halfadder_3_carry, halfadder_3_sum, halfadder_4_carry,
       halfadder_4_sum, halfadder_5_carry, halfadder_5_sum, halfadder_6_carry, halfadder_6_sum,
       halfadder_7_carry, halfadder_7_sum, halfadder_8_carry, halfadder_8_sum, halfadder_9_carry,
       halfadder_9_sum, halfadder_10_carry, halfadder_10_sum, halfadder_11_carry, halfadder_11_sum,
       halfadder_12_carry, halfadder_12_sum, halfadder_13_carry, halfadder_13_sum, halfadder_14_carry,
       halfadder_14_sum, halfadder_15_carry, halfadder_15_sum, not_1_out, or_1_out, or_2_out, xor_1_out;
  wire [7:0] controlled_buffer_2_out;

  assign controlled_buffer_1_out = Increment ? halfadder_15_carry : 1'bz;  // Controlled_Buffer controlled_buffer_1
  assign controlled_buffer_2_out = not_1_out ? BUS_in : 8'bz;  // Controlled_Buffer controlled_buffer_2
  not not_1 (not_1_out, Increment);
  or or_1 (or_1_out, BUS_to_P2, Increment);
  buf buffer_1 (buffer_1_out, controlled_buffer_2_out[0]);
  buf buffer_2 (buffer_2_out, controlled_buffer_2_out[0]);
  or or_2 (or_2_out, Increment, Bus_to_P1);
  MS_D_Latch ms_d_latch_1 (.Input(buffer_1_out), .Clock(or_1_out), .Out(Mem_Out[0]));  // open: Out_negate
  assign buffer_1_out = Increment ? halfadder_1_sum : 1'bz;  // Controlled_Buffer controlled_buffer_3
  buf buffer_3 (buffer_3_out, controlled_buffer_2_out[1]);
  HalfAdder halfadder_1 (.A(Mem_Out[0]), .B(controlled_buffer_1_out), .Sum(halfadder_1_sum), .Carry(halfadder_1_carry));
  HalfAdder halfadder_2 (.A(Increment), .B(Mem_Out[8]), .Sum(halfadder_2_sum), .Carry(halfadder_2_carry));
  assign buffer_2_out = Increment ? halfadder_2_sum : 1'bz;  // Controlled_Buffer controlled_buffer_4
  buf buffer_4 (buffer_4_out, controlled_buffer_2_out[1]);
  MS_D_Latch ms_d_latch_2 (.Input(buffer_2_out), .Clock(or_2_out), .Out(Mem_Out[8]));  // open: Out_negate
  MS_D_Latch ms_d_latch_3 (.Input(buffer_3_out), .Clock(or_1_out), .Out(Mem_Out[1]));  // open: Out_negate
  assign buffer_3_out = Increment ? halfadder_3_sum : 1'bz;  // Controlled_Buffer controlled_buffer_5
  buf buffer_5 (buffer_5_out, controlled_buffer_2_out[2]);
  HalfAdder halfadder_3 (.A(halfadder_1_carry), .B(Mem_Out[1]), .Sum(halfadder_3_sum), .Carry(halfadder_3_carry));
  HalfAdder halfadder_4 (.A(halfadder_2_carry), .B(Mem_Out[9]), .Sum(halfadder_4_sum), .Carry(halfadder_4_carry));
  assign buffer_4_out = Increment ? halfadder_4_sum : 1'bz;  // Controlled_Buffer controlled_buffer_6
  buf buffer_6 (buffer_6_out, controlled_buffer_2_out[2]);
  MS_D_Latch ms_d_latch_4 (.Input(buffer_4_out), .Clock(or_2_out), .Out(Mem_Out[9]));  // open: Out_negate
  MS_D_Latch ms_d_latch_5 (.Input(buffer_5_out), .Clock(or_1_out), .Out(Mem_Out[2]));  // open: Out_negate
  assign buffer_5_out = Increment ? halfadder_5_sum : 1'bz;  // Controlled_Buffer controlled_buffer_7
  buf buffer_7 (buffer_7_out, controlled_buffer_2_out[3]);
  HalfAdder halfadder_5 (.A(halfadder_3_carry), .B(Mem_Out[2]), .Sum(halfadder_5_sum), .Carry(halfadder_5_carry));
  HalfAdder halfadder_6 (.A(halfadder_4_carry), .B(Mem_Out[10]), .Sum(halfadder_6_sum), .Carry(halfadder_6_carry));
  buf buffer_8 (buffer_8_out, controlled_buffer_2_out[3]);
  assign buffer_6_out = Increment ? halfadder_6_sum : 1'bz;  // Controlled_Buffer controlled_buffer_8
  MS_D_Latch ms_d_latch_6 (.Input(buffer_6_out), .Clock(or_2_out), .Out(Mem_Out[10]));  // open: Out_negate
  MS_D_Latch ms_d_latch_7 (.Input(buffer_7_out), .Clock(or_1_out), .Out(Mem_Out[3]));  // open: Out_negate
  buf buffer_9 (buffer_9_out, controlled_buffer_2_out[4]);
  assign buffer_7_out = Increment ? halfadder_7_sum : 1'bz;  // Controlled_Buffer controlled_buffer_9
  HalfAdder halfadder_7 (.A(halfadder_5_carry), .B(Mem_Out[3]), .Sum(halfadder_7_sum), .Carry(halfadder_7_carry));
  HalfAdder halfadder_8 (.A(halfadder_6_carry), .B(Mem_Out[11]), .Sum(halfadder_8_sum), .Carry(halfadder_8_carry));
  assign buffer_8_out = Increment ? halfadder_8_sum : 1'bz;  // Controlled_Buffer controlled_buffer_10
  buf buffer_10 (buffer_10_out, controlled_buffer_2_out[4]);
  MS_D_Latch ms_d_latch_8 (.Input(buffer_8_out), .Clock(or_2_out), .Out(Mem_Out[11]));  // open: Out_negate
  MS_D_Latch ms_d_latch_9 (.Input(buffer_9_out), .Clock(or_1_out), .Out(Mem_Out[4]));  // open: Out_negate
  buf buffer_11 (buffer_11_out, controlled_buffer_2_out[5]);
  assign buffer_9_out = Increment ? halfadder_9_sum : 1'bz;  // Controlled_Buffer controlled_buffer_11
  HalfAdder halfadder_9 (.A(halfadder_7_carry), .B(Mem_Out[4]), .Sum(halfadder_9_sum), .Carry(halfadder_9_carry));
  HalfAdder halfadder_10 (.A(halfadder_8_carry), .B(Mem_Out[12]), .Sum(halfadder_10_sum), .Carry(halfadder_10_carry));
  buf buffer_12 (buffer_12_out, controlled_buffer_2_out[5]);
  assign buffer_10_out = Increment ? halfadder_10_sum : 1'bz;  // Controlled_Buffer controlled_buffer_12
  MS_D_Latch ms_d_latch_10 (.Input(buffer_10_out), .Clock(or_2_out), .Out(Mem_Out[12]));  // open: Out_negate
  MS_D_Latch ms_d_latch_11 (.Input(buffer_11_out), .Clock(or_1_out), .Out(Mem_Out[5]));  // open: Out_negate
  assign buffer_11_out = Increment ? halfadder_11_sum : 1'bz;  // Controlled_Buffer controlled_buffer_13
  buf buffer_13 (buffer_13_out, controlled_buffer_2_out[6]);
  HalfAdder halfadder_11 (.A(halfadder_9_carry), .B(Mem_Out[5]), .Sum(halfadder_11_sum), .Carry(halfadder_11_carry));
  HalfAdder halfadder_12 (.A(halfadder_10_carry), .B(Mem_Out[13]), .Sum(halfadder_12_sum), .Carry(halfadder_12_carry));
  buf buffer_14 (buffer_14_out, controlled_buffer_2_out[6]);
  assign buffer_12_out = Increment ? halfadder_12_sum : 1'bz;  // Controlled_Buffer controlled_buffer_14
  MS_D_Latch ms_d_latch_12 (.Input(buffer_12_out), .Clock(or_2_out), .Out(Mem_Out[13]));  // open: Out_negate
  MS_D_Latch ms_d_latch_13 (.Input(buffer_13_out), .Clock(or_1_out), .Out(Mem_Out[6]));  // open: Out_negate
  assign buffer_13_out = Increment ? halfadder_13_sum : 1'bz;  // Controlled_Buffer controlled_buffer_15
  buf buffer_15 (buffer_15_out, controlled_buffer_2_out[7]);
  HalfAdder halfadder_13 (.A(halfadder_11_carry), .B(Mem_Out[6]), .Sum(halfadder_13_sum), .Carry(halfadder_13_carry));
  HalfAdder halfadder_14 (.A(halfadder_12_carry), .B(Mem_Out[14]), .Sum(halfadder_14_sum), .Carry(halfadder_14_carry));
  assign buffer_14_out = Increment ? halfadder_14_sum : 1'bz;  // Controlled_Buffer controlled_buffer_16
  buf buffer_16 (buffer_16_out, controlled_buffer_2_out[7]);
  MS_D_Latch ms_d_latch_14 (.Input(buffer_14_out), .Clock(or_2_out), .Out(Mem_Out[14]));  // open: Out_negate
  MS_D_Latch ms_d_latch_15 (.Input(buffer_15_out), .Clock(or_1_out), .Out(Mem_Out[7]));  // open: Out_negate
  assign buffer_15_out = Increment ? xor_1_out : 1'bz;  // Controlled_Buffer controlled_buffer_17
  xor xor_1 (xor_1_out, Mem_Out[7], halfadder_13_carry);
  HalfAdder halfadder_15 (.A(halfadder_14_carry), .B(Mem_Out[15]), .Sum(halfadder_15_sum), .Carry(halfadder_15_carry));
  assign buffer_16_out = Increment ? halfadder_15_sum : 1'bz;  // Controlled_Buffer controlled_buffer_18
  MS_D_Latch ms_d_latch_16 (.Input(buffer_16_out), .Clock(or_2_out), .Out(Mem_Out[15]));  // open: Out_negate
endmodule

module ALU (
  input  [7:0] BUS,
  input  [7:0] Accumulator,
  input  [2:0] Control_Unit,
  output Set_Carry,
  output Carry,
  output [7:0] Accumulator_2
);

  wire [7:0] Adder_output, And_output_and, Inverter_output, Or_output_acc, shl_output_acc, shr_output_acc,
       Xor_output_acc;

  And And (.Input_Acc(Accumulator), .Input_Bus(BUS), .Output_AND(And_output_and));
  Or Or (.Input_Acc(Accumulator), .Input_Bus(BUS), .Output_Acc(Or_output_acc));
  Xor Xor (.Input_Acc(Accumulator), .Input_Bus(BUS), .Output_Acc(Xor_output_acc));
  shl shl (.Input_Acc(Accumulator), .Output_Acc(shl_output_acc), .Input_Bus(BUS));
  shr shr (.Input_Acc(Accumulator), .Output_Acc(shr_output_acc), .Input_Bus(BUS));
  Adder Adder (.Sub(Control_Unit[0]), .A(Accumulator), .B(BUS), .Output(Adder_output), .Carry(Carry));
  Inverter Inverter (.Input(Accumulator), .Output(Inverter_output));
  Multiplexer #(.select(3), .width(8), .enable("false")) multiplexer_1 (
    .in0(Adder_output), .in1(Adder_output), .in2(And_output_and), .in3(Or_output_acc), .in4(Xor_output_acc),
    .in5(Inverter_output), .in6(shl_output_acc), .in7(shr_output_acc), .out(Accumulator_2), .sel(Control_Unit));
  nor nor_1 (Set_Carry, Control_Unit[2], Control_Unit[1]);
endmodule

module Inverter (
  input  [7:0] Input,
  output [7:0] Output
);

  assign Output = ~Input;  // NOT_Gate not_1, 8 bits wide
endmodule

module Adder (
  input  Sub,
  input  [7:0] A,
  input  [7:0] B,
  output [7:0] Output,
  output Carry
);

  wire fulladder_1_carry_out, fulladder_2_carry_out, fulladder_3_carry_out, fulladder_4_carry_out,
       fulladder_5_carry_out, fulladder_6_carry_out, fulladder_7_carry_out, fulladder_8_carry_out, xor_1_out,
       xor_2_out, xor_3_out, xor_4_out, xor_5_out, xor_6_out, xor_7_out, xor_8_out;

  xor xor_1 (xor_1_out, B[0], Sub);
  xor xor_2 (xor_2_out, B[1], Sub);
  xor xor_3 (xor_3_out, B[2], Sub);
  xor xor_4 (xor_4_out, B[3], Sub);
  xor xor_5 (xor_5_out, B[4], Sub);
  xor xor_6 (xor_6_out, B[5], Sub);
  xor xor_7 (xor_7_out, B[6], Sub);
  xor xor_8 (xor_8_out, B[7], Sub);
  FullAdder fulladder_1 (.Carry_In(Sub), .A(A[0]), .B(xor_1_out), .Sum(Output[0]), .Carry_Out(fulladder_1_carry_out));
  FullAdder fulladder_2 (
    .Carry_In(fulladder_1_carry_out), .A(A[1]), .B(xor_2_out), .Sum(Output[1]),
    .Carry_Out(fulladder_2_carry_out));
  FullAdder fulladder_3 (
    .Carry_In(fulladder_2_carry_out), .A(A[2]), .B(xor_3_out), .Sum(Output[2]),
    .Carry_Out(fulladder_3_carry_out));
  FullAdder fulladder_4 (
    .Carry_In(fulladder_3_carry_out), .A(A[3]), .B(xor_4_out), .Sum(Output[3]),
    .Carry_Out(fulladder_4_carry_out));
  FullAdder fulladder_5 (
    .Carry_In(fulladder_4_carry_out), .A(A[4]), .B(xor_5_out), .Sum(Output[4]),
    .Carry_Out(fulladder_5_carry_out));
  FullAdder fulladder_6 (
    .Carry_In(fulladder_5_carry_out), .A(A[5]), .B(xor_6_out), .Sum(Output[5]),
    .Carry_Out(fulladder_6_carry_out));
  FullAdder fulladder_7 (
    .Carry_In(fulladder_6_carry_out), .A(A[6]), .B(xor_7_out), .Sum(Output[6]),
    .Carry_Out(fulladder_7_carry_out));
  FullAdder fulladder_8 (
    .Carry_In(fulladder_7_carry_out), .A(A[7]), .B(xor_8_out), .Sum(Output[7]),
    .Carry_Out(fulladder_8_carry_out));
  xor xor_9 (Carry, fulladder_8_carry_out, Sub);
endmodule

module FullAdder (
  input  Carry_In,
  input  A,
  input  B,
  output Sum,
  output Carry_Out
);

  wire halfadder_1_carry, halfadder_1_sum, halfadder_2_carry;

  HalfAdder halfadder_1 (.A(A), .B(B), .Sum(halfadder_1_sum), .Carry(halfadder_1_carry));
  HalfAdder halfadder_2 (.A(Carry_In), .B(halfadder_1_sum), .Sum(Sum), .Carry(halfadder_2_carry));
  or or_1 (Carry_Out, halfadder_2_carry, halfadder_1_carry);
endmodule

module HalfAdder (
  input  A,
  input  B,
  output Sum,
  output Carry
);

  xor xor_1 (Sum, A, B);
  and and_1 (Carry, A, B);
endmodule

module And (
  input  [7:0] Input_Acc,
  input  [7:0] Input_Bus,
  output [7:0] Output_AND
);

  assign Output_AND = Input_Acc & Input_Bus;  // AND_Gate and_1, 8 bits wide
endmodule

module Or (
  input  [7:0] Input_Acc,
  input  [7:0] Input_Bus,
  output [7:0] Output_Acc
);

  assign Output_Acc = Input_Acc | Input_Bus;  // OR_Gate or_1, 8 bits wide
endmodule

module Xor (
  input  [7:0] Input_Acc,
  input  [7:0] Input_Bus,
  output [7:0] Output_Acc
);

  assign Output_Acc = Input_Acc ^ Input_Bus;  // XOR_Gate xor_1, 8 bits wide
endmodule

module shl (
  input  [7:0] Input_Acc,
  input  [7:0] Input_Bus,
  output [7:0] Output_Acc
);

  wire [7:0] multiplexer_8_out;

  Multiplexer #(.select(3), .enable("false")) multiplexer_1 (
    .in0(Input_Acc[0]), .in1(1'b0), .in2(1'b0), .in3(1'b0), .in4(1'b0), .in5(1'b0), .in6(1'b0), .in7(1'b0),
    .out(multiplexer_8_out[7]), .sel(Input_Bus[2:0]));
  Multiplexer #(.select(3), .enable("false")) multiplexer_2 (
    .in0(Input_Acc[2]), .in1(Input_Acc[1]), .in2(Input_Acc[0]), .in3(1'b0), .in4(1'b0), .in5(1'b0),
    .in6(1'b0), .in7(1'b0), .out(multiplexer_8_out[5]), .sel(Input_Bus[2:0]));
  Multiplexer #(.select(3), .enable("false")) multiplexer_3 (
    .in0(Input_Acc[1]), .in1(Input_Acc[0]), .in2(1'b0), .in3(1'b0), .in4(1'b0), .in5(1'b0), .in6(1'b0),
    .in7(1'b0), .out(multiplexer_8_out[6]), .sel(Input_Bus[2:0]));
  Multiplexer #(.select(3), .enable("false")) multiplexer_4 (
    .in0(Input_Acc[3]), .in1(Input_Acc[2]), .in2(Input_Acc[1]), .in3(Input_Acc[0]), .in4(1'b0), .in5(1'b0),
    .in6(1'b0), .in7(1'b0), .out(multiplexer_8_out[4]), .sel(Input_Bus[2:0]));
  Multiplexer #(.select(3), .enable("false")) multiplexer_5 (
    .in0(Input_Acc[4]), .in1(Input_Acc[3]), .in2(Input_Acc[2]), .in3(Input_Acc[1]), .in4(Input_Acc[0]),
    .in5(1'b0), .in6(1'b0), .in7(1'b0), .out(multiplexer_8_out[3]), .sel(Input_Bus[2:0]));
  Multiplexer #(.select(3), .enable("false")) multiplexer_6 (
    .in0(Input_Acc[5]), .in1(Input_Acc[4]), .in2(Input_Acc[3]), .in3(Input_Acc[2]), .in4(Input_Acc[1]),
    .in5(Input_Acc[0]), .in6(1'b0), .in7(1'b0), .out(multiplexer_8_out[2]), .sel(Input_Bus[2:0]));
  Multiplexer #(.select(3), .enable("false")) multiplexer_7 (
    .in0(Input_Acc[6]), .in1(Input_Acc[5]), .in2(Input_Acc[4]), .in3(Input_Acc[3]), .in4(Input_Acc[2]),
    .in5(Input_Acc[1]), .in6(Input_Acc[0]), .in7(1'b0), .out(multiplexer_8_out[1]), .sel(Input_Bus[2:0]));
  Multiplexer #(.select(3), .enable("false")) multiplexer_8 (
    .in0(Input_Acc[7]), .in1(Input_Acc[6]), .in2(Input_Acc[5]), .in3(Input_Acc[4]), .in4(Input_Acc[3]),
    .in5(Input_Acc[2]), .in6(Input_Acc[1]), .in7(Input_Acc[0]), .out(multiplexer_8_out[0]),
    .sel(Input_Bus[2:0]));
  assign Output_Acc = Input_Bus[3] ? multiplexer_8_out : 8'bz;  // Controlled_Buffer controlled_buffer_1
endmodule

module shr (
  input  [7:0] Input_Acc,
  input  [7:0] Input_Bus,
  output [7:0] Output_Acc
);

  wire [7:0] multiplexer_8_out;

  Multiplexer #(.select(3), .enable("false")) multiplexer_1 (
    .in0(Input_Acc[7]), .in1(Input_Acc[7]), .in2(Input_Acc[7]), .in3(Input_Acc[7]), .in4(Input_Acc[7]),
    .in5(Input_Acc[7]), .in6(Input_Acc[7]), .in7(Input_Acc[7]), .out(multiplexer_8_out[7]),
    .sel(Input_Bus[2:0]));
  Multiplexer #(.select(3), .enable("false")) multiplexer_2 (
    .in0(Input_Acc[5]), .in1(Input_Acc[6]), .in2(Input_Acc[7]), .in3(Input_Acc[7]), .in4(Input_Acc[7]),
    .in5(Input_Acc[7]), .in6(Input_Acc[7]), .in7(Input_Acc[7]), .out(multiplexer_8_out[5]),
    .sel(Input_Bus[2:0]));
  Multiplexer #(.select(3), .enable("false")) multiplexer_3 (
    .in0(Input_Acc[6]), .in1(Input_Acc[7]), .in2(Input_Acc[7]), .in3(Input_Acc[7]), .in4(Input_Acc[7]),
    .in5(Input_Acc[7]), .in6(Input_Acc[7]), .in7(Input_Acc[7]), .out(multiplexer_8_out[6]),
    .sel(Input_Bus[2:0]));
  Multiplexer #(.select(3), .enable("false")) multiplexer_4 (
    .in0(Input_Acc[4]), .in1(Input_Acc[5]), .in2(Input_Acc[6]), .in3(Input_Acc[7]), .in4(Input_Acc[7]),
    .in5(Input_Acc[7]), .in6(Input_Acc[7]), .in7(Input_Acc[7]), .out(multiplexer_8_out[4]),
    .sel(Input_Bus[2:0]));
  Multiplexer #(.select(3), .enable("false")) multiplexer_5 (
    .in0(Input_Acc[3]), .in1(Input_Acc[4]), .in2(Input_Acc[5]), .in3(Input_Acc[6]), .in4(Input_Acc[7]),
    .in5(Input_Acc[7]), .in6(Input_Acc[7]), .in7(Input_Acc[7]), .out(multiplexer_8_out[3]),
    .sel(Input_Bus[2:0]));
  Multiplexer #(.select(3), .enable("false")) multiplexer_6 (
    .in0(Input_Acc[2]), .in1(Input_Acc[3]), .in2(Input_Acc[4]), .in3(Input_Acc[5]), .in4(Input_Acc[6]),
    .in5(Input_Acc[7]), .in6(Input_Acc[7]), .in7(Input_Acc[7]), .out(multiplexer_8_out[2]),
    .sel(Input_Bus[2:0]));
  Multiplexer #(.select(3), .enable("false")) multiplexer_7 (
    .in0(Input_Acc[1]), .in1(Input_Acc[2]), .in2(Input_Acc[3]), .in3(Input_Acc[4]), .in4(Input_Acc[5]),
    .in5(Input_Acc[6]), .in6(Input_Acc[7]), .in7(Input_Acc[7]), .out(multiplexer_8_out[1]),
    .sel(Input_Bus[2:0]));
  Multiplexer #(.select(3), .enable("false")) multiplexer_8 (
    .in0(Input_Acc[0]), .in1(Input_Acc[1]), .in2(Input_Acc[2]), .in3(Input_Acc[3]), .in4(Input_Acc[4]),
    .in5(Input_Acc[5]), .in6(Input_Acc[6]), .in7(Input_Acc[7]), .out(multiplexer_8_out[0]),
    .sel(Input_Bus[2:0]));
  assign Output_Acc = Input_Bus[3] ? multiplexer_8_out : 8'bz;  // Controlled_Buffer controlled_buffer_1
endmodule

module RS_getaktet (
  input  Set,
  input  Clock,
  input  Reset,
  output Out,
  output Out_negate
);

  wire nand_1_out, nand_2_out;

  nand nand_1 (nand_1_out, Set, Clock);
  nand nand_2 (nand_2_out, Clock, Reset);
  nand nand_3 (Out, nand_1_out, Out_negate);
  nand nand_4 (Out_negate, Out, nand_2_out);
endmodule

module RS_ungetaktet (
  input  Out,
  input  R,
  input  S,
  input  Out_negate
);

  nor nor_1 (Out, Out_negate, R);
  nor nor_2 (Out_negate, S, Out);
endmodule

module MS_D_Latch (
  input  Input,
  input  Clock,
  output Out,
  output Out_negate
);

  wire nand_1_out, nand_2_out, nand_3_out, nand_4_out, nand_5_out, nand_6_out, not_1_out;

  nand nand_1 (nand_1_out, Input, Clock);
  nand nand_2 (nand_2_out, nand_1_out, Clock);
  not not_1 (not_1_out, Clock);
  nand nand_3 (nand_3_out, nand_1_out, nand_4_out);
  nand nand_4 (nand_4_out, nand_3_out, nand_2_out);
  nand nand_5 (nand_5_out, nand_3_out, not_1_out);
  nand nand_6 (nand_6_out, nand_5_out, not_1_out);
  nand nand_7 (Out, nand_5_out, Out_negate);
  nand nand_8 (Out_negate, Out, nand_6_out);
endmodule

module MemoryCell (
  input  [7:0] Input,
  input  Set,
  output [7:0] Output
);

  MS_D_Latch ms_d_latch_1 (.Input(Input[0]), .Clock(Set), .Out(Output[0]));  // open: Out_negate
  MS_D_Latch ms_d_latch_2 (.Input(Input[1]), .Clock(Set), .Out(Output[1]));  // open: Out_negate
  MS_D_Latch ms_d_latch_3 (.Input(Input[2]), .Clock(Set), .Out(Output[2]));  // open: Out_negate
  MS_D_Latch ms_d_latch_4 (.Input(Input[3]), .Clock(Set), .Out(Output[3]));  // open: Out_negate
  MS_D_Latch ms_d_latch_5 (.Input(Input[4]), .Clock(Set), .Out(Output[4]));  // open: Out_negate
  MS_D_Latch ms_d_latch_6 (.Input(Input[5]), .Clock(Set), .Out(Output[5]));  // open: Out_negate
  MS_D_Latch ms_d_latch_7 (.Input(Input[6]), .Clock(Set), .Out(Output[6]));  // open: Out_negate
  MS_D_Latch ms_d_latch_8 (.Input(Input[7]), .Clock(Set), .Out(Output[7]));  // open: Out_negate
endmodule

module Tests (
  input  Sub,
  input  [7:0] A,
  input  [7:0] B,
  input  [7:0] in_4,
  input  [7:0] in_5,
  output [7:0] out_6,
  output [7:0] out_7,
  output out_8,
  output [7:0] out_9,
  output [7:0] out_10
);

  Or or_1 (.Input_Acc(in_5), .Input_Bus(in_4), .Output_Acc(out_10));
  Inverter inverter_1 (.Input(8'hfe), .Output(out_6));
  Adder adder_1 (.Sub(Sub), .A(A), .B(B), .Output(out_7), .Carry(out_8));
  Xor xor_1 (.Input_Acc(in_4), .Input_Bus(in_5), .Output_Acc(out_9));
endmodule
